# Fritzing sketch Circuit2 (saved by Fritzing 0.6.3b)
breadboards: 1

parts:
  Arduino1 = Arduino
  DAC1 = IC, DIP package, 8 pins [chip_label=IC spacing=300mil]
  DAC2 = IC, DIP package, 8 pins [chip_label=IC spacing=300mil]
  Q1 = NPN-Transistor [package="TO92 [THT]"]
  R1 = Resistor [tolerance=±5% resistance=220 package=THT]
  R2 = Resistor [tolerance=±5% resistance=100k package=THT]

nets:
  N1: Arduino1.GND, DAC1.pin7, DAC2.pin7, Q1.E
  N2: Arduino1.D13, DAC1.pin3, DAC2.pin3
  N3: Arduino1.D11, DAC1.pin4, DAC2.pin4
  N4: Arduino1.D10, DAC2.pin2
  N5: Arduino1.D9, DAC1.pin2
  N6: Arduino1.+5V, DAC1.pin1, DAC1.pin6, DAC2.pin1, DAC2.pin6
  N7: Arduino1.A0, Q1.C, R1.Pin_1
  N8: Arduino1.A1, DAC1.pin8, R1.Pin_0
  N9: Arduino1.A2, Q1.B, R2.Pin_1
  N10: Arduino1.A3, DAC2.pin8, R2.Pin_0
